# Fritzing sketch Breadbroad_pinout (saved by Fritzing 0.9.10b)
breadboards: 1

parts:
  7_Segment5 = 7 Segment Display
  7_Segment6 = 7 Segment Display
  IC1_PWR = 74LS32 [package="DIP (Dual Inline) [THT]"]  # not connected
  IC1_4 = 74LS32 [package="DIP (Dual Inline) [THT]"]  # not connected
  IC1_3 = 74LS32 [package="DIP (Dual Inline) [THT]"]  # not connected
  IC1_2 = 74LS32 [package="DIP (Dual Inline) [THT]"]  # not connected
  IC1_1 = 74LS32 [package="DIP (Dual Inline) [THT]"]  # not connected
  IC1 = IC, DIP package, 16 pins [chip_label=74LS47]
  IC2 = IC, DIP package, 16 pins [chip_label=74LS47]
  IC7 = IC, DIP package, 16 pins [chip_label=74LS190]
  IC8 = IC, DIP package, 16 pins [chip_label=74LS190]
  IC4 = IC, DIP package, 14 pins [chip_label=74LS08]
  IC9 = IC, DIP package, 14 pins [chip_label=74LS08]
  IC10_PWR = 74LS32 [package="DIP (Dual Inline) [THT]"]  # not connected
  IC10_4 = 74LS32 [package="DIP (Dual Inline) [THT]"]  # not connected
  IC10_3 = 74LS32 [package="DIP (Dual Inline) [THT]"]  # not connected
  IC10_2 = 74LS32 [package="DIP (Dual Inline) [THT]"]  # not connected
  IC10_1 = 74LS32 [package="DIP (Dual Inline) [THT]"]  # not connected
  IC10 = IC, DIP package, 14 pins [chip_label=74LS04]

nets:
  N1: 7_Segment5.Segment_E, IC2.pin9
  N2: 7_Segment5.Segment_D, IC2.pin10
  N3: 7_Segment5.common_cathode, 7_Segment6.common_cathode, IC1.pin16, IC2.pin16, IC7.pin16, IC8.pin16, IC4.pin14, IC9.pin14, IC10.pin14
  N4: 7_Segment5.Segment_C, IC2.pin11
  N5: 7_Segment5.Segment_B, IC2.pin12
  N6: 7_Segment5.Segment_A, IC2.pin13
  N7: 7_Segment5.Segment_F, IC2.pin15
  N8: 7_Segment5.Segment_G, IC2.pin14
  N9: 7_Segment6.Segment_E, IC1.pin9
  N10: 7_Segment6.Segment_D, IC1.pin10
  N11: 7_Segment6.Segment_C, IC1.pin11
  N12: 7_Segment6.Segment_B, IC1.pin12
  N13: 7_Segment6.Segment_A, IC1.pin13
  N14: 7_Segment6.Segment_F, IC1.pin15
  N15: 7_Segment6.Segment_G, IC1.pin14
  N16: IC1.pin1, IC8.pin2, IC4.pin5
  N17: IC1.pin2, IC8.pin6
  N18: IC1.pin6, IC8.pin7
  N19: IC1.pin7, IC8.pin3, IC4.pin4
  N20: IC1.pin8, IC2.pin1, IC2.pin2, IC2.pin6, IC2.pin8, IC7.pin8, IC8.pin8, IC4.pin7, IC9.pin7, IC10.pin7
  N21: IC2.pin7, IC7.pin3, IC4.pin1
  N22: IC4.pin2, IC4.pin6
  N23: IC4.pin3, IC10.pin1

custom parts:
  74LS32: 2 input OR gate
  74LS32: 2 input OR gate
  74LS32: 2 input OR gate
  74LS32: 2 input OR gate
  74LS32: 2 input OR gate
